# Fritzing sketch lesson_2 (saved by Fritzing 0.9.3b)
breadboards: 1

parts:
  U1 = ESP32S-HiLetgo [part_number=ESP32S-HiLetgo]
  ZS-042_RTC1 = ZS-042 RTC Module
  Part1 = GY-BMEP280 Barometric Pressure Sensor - Breakout

nets:
  VIN: U1.VIN, ZS-042_RTC1.GND, Part1.SCL
  N1: U1.GPIO6, ZS-042_RTC1.VCC, Part1.SDA
  N2: U1.GPIO3, ZS-042_RTC1.SDA, Part1.VCC
  N3: U1.GPIO23, ZS-042_RTC1.SCL, Part1.GND

custom parts:
  ESP32S-HiLetgo: HiLetgo ESP-WROOM-32 ESP32 ESP-32S Development Board 2.4GHz Dual-Mode WiFi + Bluetooth Dual Cores Microcontroller The ESP32 integrated with Antenna switches, RF Balun, power amplifiers, low-noise amplifiers, filters, and management modules, and the entire solution occupies the least area of PCB. 2.4 GHz Wi-Fi plus Bluetooth dual-mode chip, with TSMC Ultra-low power consumption 40nm technology,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
  GY-BMEP280 Barometric Pressure Sensor - Breakout: The BME280 is a chip which was originally designed for the next generation of smartphones. It is made up of a very accurate pressure sensor and an associated temperature sensor which helps calibrate the pressure readings. And just for fun they threw in a pretty solid humidity sensor in there as well! So with an I2C connection you have access to enough weather data to make some pretty good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
